// Logisim project 8 bit logicSim.circ as structural Verilog: 7 circuits, main circuit main
module main (
  input  in_1,
  input  in_2,
  input  in_3,
  input  in_4,
  input  in_5,
  input  in_6,
  input  in_7,
  input  in_8,
  input  in_9,
  input  in_10,
  input  in_11,
  input  in_12,
  input  in_13,
  input  in_14,
  input  in_15,
  input  in_16,
  input  in_17,
  input  in_18,
  input  in_19,
  input  in_20,
  input  in_21,
  input  in_22,
  input  in_23,
  input  in_24,
  input  in_25,
  input  in_26,
  input  in_27,
  input  in_28,
  input  in_29,
  output out_30,
  output out_31,
  output out_32,
  output out_33,
  output out_34,
  output out_35,
  output out_36,
  output out_37
);

  wire button_1_out, button_2_out, clock_1_out, cpu_1_out_26, cpu_1_out_27, cpu_1_out_28, cpu_1_out_29,
       cpu_1_out_30, cpu_1_out_31, cpu_1_out_32, cpu_1_out_33;

  Clock clock_1 (.out(clock_1_out));
  Button button_1 (.out(button_1_out));
  Button button_2 (.out(button_2_out));
  CPU cpu_1 (
    .in_1(in_1), .in_2(in_2), .in_3(in_3), .in_4(in_4), .in_5(button_1_out), .in_6(in_5), .in_7(in_6),
    .in_8(in_7), .in_9(in_8), .in_10(in_9), .in_11(in_10), .in_12(clock_1_out), .in_13(in_12), .in_14(in_25),
    .in_15(in_26), .in_16(in_13), .in_17(button_2_out), .in_18(in_14), .in_19(in_16), .in_20(in_18),
    .in_21(in_20), .in_22(in_11), .in_23(in_22), .in_24(in_24), .in_25(in_19), .out_26(cpu_1_out_26),
    .out_27(cpu_1_out_27), .out_28(cpu_1_out_28), .out_29(cpu_1_out_29), .out_30(cpu_1_out_30),
    .out_31(cpu_1_out_31), .out_32(cpu_1_out_32), .out_33(cpu_1_out_33));
  _8_Bit_RAM u_8_bit_ram_1 (
    .in_1(cpu_1_out_26), .in_2(cpu_1_out_27), .in_3(cpu_1_out_28), .in_4(cpu_1_out_29), .in_5(cpu_1_out_30),
    .in_6(cpu_1_out_31), .in_7(cpu_1_out_32), .in_8(cpu_1_out_33), .in_9(in_15), .in_10(in_17),
    .in_11(in_21), .in_12(in_23), .CS(in_27), .RD(in_28), .EO(in_29), .out_16(out_37), .out_17(out_36),
    .out_18(out_35), .out_19(out_34), .out_20(out_33), .out_21(out_32), .out_22(out_31), .out_23(out_30));
endmodule

module Register_A (
  input  in_1,
  input  in_2,
  input  in_3,
  input  in_4,
  input  in_5,
  input  in_6,
  input  in_7,
  input  in_8,
  input  in_9,
  input  in_10,
  input  in_11,
  input  in_12,
  output out_13,
  output out_14,
  output out_15,
  output out_16,
  output out_17,
  output out_18,
  output out_19,
  output out_20
);

  wire and_1_out, and_2_out, and_3_out, and_4_out, and_5_out, and_6_out, and_7_out, and_8_out, and_9_out,
       and_10_out, and_11_out, and_12_out, and_13_out, and_14_out, and_15_out, and_16_out, and_17_out,
       and_18_out, and_19_out, and_20_out, and_21_out, and_22_out, and_23_out, and_24_out, and_25_out,
       and_26_out, and_27_out, and_28_out, and_29_out, and_30_out, and_31_out, and_32_out, and_33_out,
       controlled_buffer_9_out, controlled_buffer_10_out, controlled_buffer_11_out, controlled_buffer_12_out,
       controlled_buffer_13_out, controlled_buffer_14_out, controlled_buffer_15_out,
       controlled_buffer_16_out, nor_1_out, nor_2_out, nor_3_out, nor_4_out, nor_5_out, nor_6_out, nor_7_out,
       nor_8_out, nor_9_out, nor_10_out, nor_11_out, nor_12_out, nor_13_out, nor_14_out, nor_15_out,
       nor_16_out, not_1_out, not_2_out, not_3_out, not_4_out, not_5_out, not_6_out, not_7_out, not_8_out,
       not_9_out, not_10_out, not_11_out, not_12_out, not_13_out, not_14_out, not_15_out, not_16_out,
       or_1_out, or_2_out, or_3_out, or_4_out, or_5_out, or_6_out, or_7_out, or_8_out;

  not not_1 (not_1_out, in_2);
  not not_2 (not_2_out, in_2);
  not not_3 (not_3_out, in_2);
  not not_4 (not_4_out, in_2);
  not not_5 (not_5_out, in_2);
  not not_6 (not_6_out, in_2);
  not not_7 (not_7_out, in_2);
  not not_8 (not_8_out, in_2);
  and and_1 (and_1_out, nor_1_out, not_1_out);
  and and_2 (and_2_out, in_2, controlled_buffer_9_out);
  and and_3 (and_3_out, nor_3_out, not_2_out);
  and and_4 (and_4_out, in_2, controlled_buffer_10_out);
  and and_5 (and_5_out, nor_5_out, not_3_out);
  and and_6 (and_6_out, in_2, controlled_buffer_11_out);
  and and_7 (and_7_out, nor_7_out, not_4_out);
  and and_8 (and_8_out, in_2, controlled_buffer_12_out);
  and and_9 (and_9_out, nor_9_out, not_5_out);
  and and_10 (and_10_out, in_2, controlled_buffer_13_out);
  and and_11 (and_11_out, nor_11_out, not_6_out);
  and and_12 (and_12_out, in_2, controlled_buffer_14_out);
  and and_13 (and_13_out, nor_13_out, not_7_out);
  and and_14 (and_14_out, in_2, controlled_buffer_15_out);
  and and_15 (and_15_out, nor_15_out, not_8_out);
  and and_16 (and_16_out, in_2, controlled_buffer_16_out);
  or or_1 (or_1_out, and_1_out, and_2_out);
  or or_2 (or_2_out, and_3_out, and_4_out);
  or or_3 (or_3_out, and_5_out, and_6_out);
  or or_4 (or_4_out, and_7_out, and_8_out);
  or or_5 (or_5_out, and_9_out, and_10_out);
  or or_6 (or_6_out, and_11_out, and_12_out);
  or or_7 (or_7_out, and_13_out, and_14_out);
  or or_8 (or_8_out, and_15_out, and_16_out);
  and and_17 (and_17_out, in_1, in_2);
  not not_9 (not_9_out, or_1_out);
  not not_10 (not_10_out, or_2_out);
  not not_11 (not_11_out, or_3_out);
  not not_12 (not_12_out, or_4_out);
  not not_13 (not_13_out, or_5_out);
  not not_14 (not_14_out, or_6_out);
  not not_15 (not_15_out, or_7_out);
  not not_16 (not_16_out, or_8_out);
  and and_18 (and_18_out, not_9_out, and_17_out);
  and and_19 (and_19_out, and_17_out, or_1_out);
  and and_20 (and_20_out, not_10_out, and_17_out);
  and and_21 (and_21_out, and_17_out, or_2_out);
  and and_22 (and_22_out, not_11_out, and_17_out);
  and and_23 (and_23_out, and_17_out, or_3_out);
  and and_24 (and_24_out, not_12_out, and_17_out);
  and and_25 (and_25_out, and_17_out, or_4_out);
  and and_26 (and_26_out, not_13_out, and_17_out);
  and and_27 (and_27_out, and_17_out, or_5_out);
  and and_28 (and_28_out, not_14_out, and_17_out);
  and and_29 (and_29_out, and_17_out, or_6_out);
  and and_30 (and_30_out, not_15_out, and_17_out);
  and and_31 (and_31_out, and_17_out, or_7_out);
  and and_32 (and_32_out, not_16_out, and_17_out);
  and and_33 (and_33_out, and_17_out, or_8_out);
  nor nor_1 (nor_1_out, and_18_out, nor_2_out);
  nor nor_2 (nor_2_out, nor_1_out, and_19_out);
  nor nor_3 (nor_3_out, and_20_out, nor_4_out);
  nor nor_4 (nor_4_out, nor_3_out, and_21_out);
  nor nor_5 (nor_5_out, and_22_out, nor_6_out);
  nor nor_6 (nor_6_out, nor_5_out, and_23_out);
  nor nor_7 (nor_7_out, and_24_out, nor_8_out);
  nor nor_8 (nor_8_out, nor_7_out, and_25_out);
  nor nor_9 (nor_9_out, and_26_out, nor_10_out);
  nor nor_10 (nor_10_out, nor_9_out, and_27_out);
  nor nor_11 (nor_11_out, and_28_out, nor_12_out);
  nor nor_12 (nor_12_out, nor_11_out, and_29_out);
  nor nor_13 (nor_13_out, and_30_out, nor_14_out);
  nor nor_14 (nor_14_out, nor_13_out, and_31_out);
  nor nor_15 (nor_15_out, and_32_out, nor_16_out);
  nor nor_16 (nor_16_out, nor_15_out, and_33_out);
  assign out_13 = in_3 ? nor_1_out : 1'bz;  // Controlled_Buffer controlled_buffer_1
  assign out_14 = in_3 ? nor_3_out : 1'bz;  // Controlled_Buffer controlled_buffer_2
  assign out_15 = in_3 ? nor_5_out : 1'bz;  // Controlled_Buffer controlled_buffer_3
  assign out_16 = in_3 ? nor_7_out : 1'bz;  // Controlled_Buffer controlled_buffer_4
  assign out_17 = in_3 ? nor_9_out : 1'bz;  // Controlled_Buffer controlled_buffer_5
  assign out_18 = in_3 ? nor_11_out : 1'bz;  // Controlled_Buffer controlled_buffer_6
  assign out_19 = in_3 ? nor_13_out : 1'bz;  // Controlled_Buffer controlled_buffer_7
  assign out_20 = in_3 ? nor_15_out : 1'bz;  // Controlled_Buffer controlled_buffer_8
  assign controlled_buffer_9_out = in_4 ? in_5 : 1'bz;  // Controlled_Buffer controlled_buffer_9
  assign controlled_buffer_10_out = in_4 ? in_6 : 1'bz;  // Controlled_Buffer controlled_buffer_10
  assign controlled_buffer_11_out = in_4 ? in_7 : 1'bz;  // Controlled_Buffer controlled_buffer_11
  assign controlled_buffer_12_out = in_4 ? in_8 : 1'bz;  // Controlled_Buffer controlled_buffer_12
  assign controlled_buffer_13_out = in_4 ? in_9 : 1'bz;  // Controlled_Buffer controlled_buffer_13
  assign controlled_buffer_14_out = in_4 ? in_10 : 1'bz;  // Controlled_Buffer controlled_buffer_14
  assign controlled_buffer_15_out = in_4 ? in_11 : 1'bz;  // Controlled_Buffer controlled_buffer_15
  assign controlled_buffer_16_out = in_4 ? in_12 : 1'bz;  // Controlled_Buffer controlled_buffer_16
endmodule

module Register_B (
  input  in_1,
  input  in_2,
  input  in_3,
  input  in_4,
  input  in_5,
  input  in_6,
  input  in_7,
  input  in_8,
  input  in_9,
  input  in_10,
  input  in_11,
  input  in_12,
  input  in_13,
  output out_14,
  output out_15,
  output out_16,
  output out_17,
  output out_18,
  output out_19,
  output out_20,
  output out_21
);

  wire and_1_out, and_2_out, and_3_out, and_4_out, and_5_out, and_6_out, and_7_out, and_8_out, and_9_out,
       and_10_out, and_11_out, and_12_out, and_13_out, and_14_out, and_15_out, and_16_out, and_17_out,
       and_18_out, and_19_out, and_20_out, and_21_out, and_22_out, and_23_out, and_24_out, and_25_out,
       and_26_out, and_27_out, and_28_out, and_29_out, and_30_out, and_31_out, and_32_out, and_33_out,
       controlled_buffer_1_out, controlled_buffer_2_out, controlled_buffer_3_out, controlled_buffer_4_out,
       controlled_buffer_5_out, controlled_buffer_6_out, controlled_buffer_7_out, controlled_buffer_8_out,
       controlled_buffer_9_out, controlled_buffer_10_out, controlled_buffer_11_out, controlled_buffer_12_out,
       controlled_buffer_13_out, controlled_buffer_14_out, controlled_buffer_15_out,
       controlled_buffer_16_out, nor_1_out, nor_2_out, nor_3_out, nor_4_out, nor_5_out, nor_6_out, nor_7_out,
       nor_8_out, nor_9_out, nor_10_out, nor_11_out, nor_12_out, nor_13_out, nor_14_out, nor_15_out,
       nor_16_out, not_1_out, not_2_out, not_3_out, not_4_out, not_5_out, not_6_out, not_7_out, not_8_out,
       not_9_out, not_10_out, not_11_out, not_12_out, not_13_out, not_14_out, not_15_out, not_16_out,
       or_1_out, or_2_out, or_3_out, or_4_out, or_5_out, or_6_out, or_7_out, or_8_out;

  not not_1 (not_1_out, in_2);
  not not_2 (not_2_out, in_2);
  not not_3 (not_3_out, in_2);
  not not_4 (not_4_out, in_2);
  not not_5 (not_5_out, in_2);
  not not_6 (not_6_out, in_2);
  not not_7 (not_7_out, in_2);
  not not_8 (not_8_out, in_2);
  and and_1 (and_1_out, nor_9_out, not_1_out);
  and and_2 (and_2_out, in_2, controlled_buffer_9_out);
  and and_3 (and_3_out, nor_10_out, not_2_out);
  and and_4 (and_4_out, in_2, controlled_buffer_10_out);
  and and_5 (and_5_out, nor_11_out, not_3_out);
  and and_6 (and_6_out, in_2, controlled_buffer_11_out);
  and and_7 (and_7_out, nor_12_out, not_4_out);
  and and_8 (and_8_out, in_2, controlled_buffer_12_out);
  and and_9 (and_9_out, nor_13_out, not_5_out);
  and and_10 (and_10_out, in_2, controlled_buffer_13_out);
  and and_11 (and_11_out, nor_14_out, not_6_out);
  and and_12 (and_12_out, in_2, controlled_buffer_14_out);
  and and_13 (and_13_out, nor_15_out, not_7_out);
  and and_14 (and_14_out, in_2, controlled_buffer_15_out);
  and and_15 (and_15_out, nor_16_out, not_8_out);
  and and_16 (and_16_out, in_2, controlled_buffer_16_out);
  and and_17 (and_17_out, in_1, in_2);
  or or_1 (or_1_out, and_1_out, and_2_out);
  or or_2 (or_2_out, and_3_out, and_4_out);
  or or_3 (or_3_out, and_5_out, and_6_out);
  or or_4 (or_4_out, and_7_out, and_8_out);
  or or_5 (or_5_out, and_9_out, and_10_out);
  or or_6 (or_6_out, and_11_out, and_12_out);
  or or_7 (or_7_out, and_13_out, and_14_out);
  or or_8 (or_8_out, and_15_out, and_16_out);
  not not_9 (not_9_out, or_1_out);
  not not_10 (not_10_out, or_2_out);
  not not_11 (not_11_out, or_3_out);
  not not_12 (not_12_out, or_4_out);
  not not_13 (not_13_out, or_5_out);
  not not_14 (not_14_out, or_6_out);
  not not_15 (not_15_out, or_7_out);
  not not_16 (not_16_out, or_8_out);
  and and_18 (and_18_out, not_9_out, and_17_out);
  and and_19 (and_19_out, and_17_out, or_1_out);
  and and_20 (and_20_out, not_10_out, and_17_out);
  and and_21 (and_21_out, and_17_out, or_2_out);
  and and_22 (and_22_out, not_11_out, and_17_out);
  and and_23 (and_23_out, and_17_out, or_3_out);
  and and_24 (and_24_out, not_12_out, and_17_out);
  and and_25 (and_25_out, and_17_out, or_4_out);
  and and_26 (and_26_out, not_13_out, and_17_out);
  and and_27 (and_27_out, and_17_out, or_5_out);
  and and_28 (and_28_out, not_14_out, and_17_out);
  and and_29 (and_29_out, and_17_out, or_6_out);
  and and_30 (and_30_out, not_15_out, and_17_out);
  and and_31 (and_31_out, and_17_out, or_7_out);
  and and_32 (and_32_out, not_16_out, and_17_out);
  and and_33 (and_33_out, and_17_out, or_8_out);
  nor nor_1 (nor_1_out, nor_9_out, and_19_out);
  nor nor_2 (nor_2_out, nor_10_out, and_21_out);
  nor nor_3 (nor_3_out, nor_11_out, and_23_out);
  nor nor_4 (nor_4_out, nor_12_out, and_25_out);
  nor nor_5 (nor_5_out, nor_13_out, and_27_out);
  nor nor_6 (nor_6_out, nor_14_out, and_29_out);
  nor nor_7 (nor_7_out, nor_15_out, and_31_out);
  nor nor_8 (nor_8_out, nor_16_out, and_33_out);
  nor nor_9 (nor_9_out, and_18_out, nor_1_out);
  nor nor_10 (nor_10_out, and_20_out, nor_2_out);
  nor nor_11 (nor_11_out, and_22_out, nor_3_out);
  nor nor_12 (nor_12_out, and_24_out, nor_4_out);
  nor nor_13 (nor_13_out, and_26_out, nor_5_out);
  nor nor_14 (nor_14_out, and_28_out, nor_6_out);
  nor nor_15 (nor_15_out, and_30_out, nor_7_out);
  nor nor_16 (nor_16_out, and_32_out, nor_8_out);
  assign controlled_buffer_1_out = in_3 ? nor_9_out : 1'bz;  // Controlled_Buffer controlled_buffer_1
  assign controlled_buffer_2_out = in_3 ? nor_10_out : 1'bz;  // Controlled_Buffer controlled_buffer_2
  assign controlled_buffer_3_out = in_3 ? nor_11_out : 1'bz;  // Controlled_Buffer controlled_buffer_3
  assign controlled_buffer_4_out = in_3 ? nor_12_out : 1'bz;  // Controlled_Buffer controlled_buffer_4
  assign controlled_buffer_5_out = in_3 ? nor_13_out : 1'bz;  // Controlled_Buffer controlled_buffer_5
  assign controlled_buffer_6_out = in_3 ? nor_14_out : 1'bz;  // Controlled_Buffer controlled_buffer_6
  assign controlled_buffer_7_out = in_3 ? nor_15_out : 1'bz;  // Controlled_Buffer controlled_buffer_7
  assign controlled_buffer_8_out = in_3 ? nor_16_out : 1'bz;  // Controlled_Buffer controlled_buffer_8
  assign controlled_buffer_9_out = in_4 ? in_5 : 1'bz;  // Controlled_Buffer controlled_buffer_9
  assign controlled_buffer_10_out = in_4 ? in_6 : 1'bz;  // Controlled_Buffer controlled_buffer_10
  assign controlled_buffer_11_out = in_4 ? in_7 : 1'bz;  // Controlled_Buffer controlled_buffer_11
  assign controlled_buffer_12_out = in_4 ? in_8 : 1'bz;  // Controlled_Buffer controlled_buffer_12
  assign controlled_buffer_13_out = in_4 ? in_9 : 1'bz;  // Controlled_Buffer controlled_buffer_13
  assign controlled_buffer_14_out = in_4 ? in_10 : 1'bz;  // Controlled_Buffer controlled_buffer_14
  assign controlled_buffer_15_out = in_4 ? in_11 : 1'bz;  // Controlled_Buffer controlled_buffer_15
  assign controlled_buffer_16_out = in_4 ? in_12 : 1'bz;  // Controlled_Buffer controlled_buffer_16
  xor xor_1 (out_14, controlled_buffer_1_out, in_13);
  xor xor_2 (out_15, controlled_buffer_2_out, in_13);
  xor xor_3 (out_16, controlled_buffer_3_out, in_13);
  xor xor_4 (out_17, controlled_buffer_4_out, in_13);
  xor xor_5 (out_18, controlled_buffer_5_out, in_13);
  xor xor_6 (out_19, controlled_buffer_6_out, in_13);
  xor xor_7 (out_20, controlled_buffer_7_out, in_13);
  xor xor_8 (out_21, controlled_buffer_8_out, in_13);
endmodule

module ALU (
  input  in_1,
  input  in_2,
  input  in_3,
  input  in_4,
  input  in_5,
  input  in_6,
  input  in_7,
  input  in_8,
  input  in_9,
  input  in_10,
  input  in_11,
  input  in_12,
  input  in_13,
  input  in_14,
  input  in_15,
  input  in_16,
  input  in_17,
  input  in_18,
  output out_19,
  output out_20,
  output out_21,
  output out_22,
  output out_23,
  output out_24,
  output out_25,
  output out_26,
  output out_27
);

  wire and_1_out, and_2_out, and_3_out, and_4_out, and_5_out, and_6_out, and_7_out, and_8_out, and_9_out,
       and_10_out, and_11_out, and_12_out, and_13_out, and_14_out, and_15_out, and_16_out, xor_1_out,
       xor_2_out, xor_3_out, xor_4_out, xor_5_out, xor_6_out, xor_7_out, xor_8_out, xor_9_out, xor_10_out,
       xor_11_out, xor_12_out, xor_13_out, xor_14_out, xor_15_out, xor_16_out, xor_17_out, xor_18_out,
       xor_19_out, xor_20_out, xor_21_out, xor_22_out, xor_23_out;

  xor xor_1 (xor_1_out, in_1, in_2);
  and and_1 (and_1_out, in_2, in_1);
  xor xor_2 (xor_2_out, in_4, in_5);
  and and_2 (and_2_out, in_5, in_4);
  xor xor_3 (xor_3_out, in_6, in_7);
  and and_3 (and_3_out, in_7, in_6);
  xor xor_4 (xor_4_out, in_8, in_9);
  and and_4 (and_4_out, in_9, in_8);
  xor xor_5 (xor_5_out, in_10, in_11);
  and and_5 (and_5_out, in_11, in_10);
  xor xor_6 (xor_6_out, in_12, in_13);
  and and_6 (and_6_out, in_13, in_12);
  xor xor_7 (xor_7_out, in_15, in_16);
  and and_7 (and_7_out, in_16, in_15);
  xor xor_8 (xor_8_out, in_17, in_18);
  and and_8 (and_8_out, in_18, in_17);
  xor xor_9 (xor_9_out, xor_1_out, in_3);
  and and_9 (and_9_out, in_3, xor_1_out);
  xor xor_10 (xor_10_out, xor_2_out, xor_17_out);
  and and_10 (and_10_out, xor_17_out, xor_2_out);
  xor xor_11 (xor_11_out, xor_3_out, xor_18_out);
  and and_11 (and_11_out, xor_18_out, xor_3_out);
  xor xor_12 (xor_12_out, xor_4_out, xor_19_out);
  and and_12 (and_12_out, xor_19_out, xor_4_out);
  xor xor_13 (xor_13_out, xor_5_out, xor_20_out);
  and and_13 (and_13_out, xor_20_out, xor_5_out);
  xor xor_14 (xor_14_out, xor_6_out, xor_21_out);
  and and_14 (and_14_out, xor_21_out, xor_6_out);
  xor xor_15 (xor_15_out, xor_7_out, xor_22_out);
  and and_15 (and_15_out, xor_22_out, xor_7_out);
  xor xor_16 (xor_16_out, xor_8_out, xor_23_out);
  and and_16 (and_16_out, xor_23_out, xor_8_out);
  xor xor_17 (xor_17_out, and_9_out, and_1_out);
  xor xor_18 (xor_18_out, and_10_out, and_2_out);
  xor xor_19 (xor_19_out, and_11_out, and_3_out);
  xor xor_20 (xor_20_out, and_12_out, and_4_out);
  xor xor_21 (xor_21_out, and_13_out, and_5_out);
  xor xor_22 (xor_22_out, and_14_out, and_6_out);
  xor xor_23 (xor_23_out, and_15_out, and_7_out);
  xor xor_24 (out_27, and_16_out, and_8_out);
  assign out_19 = in_14 ? xor_9_out : 1'bz;  // Controlled_Buffer controlled_buffer_1
  assign out_20 = in_14 ? xor_10_out : 1'bz;  // Controlled_Buffer controlled_buffer_2
  assign out_21 = in_14 ? xor_11_out : 1'bz;  // Controlled_Buffer controlled_buffer_3
  assign out_22 = in_14 ? xor_12_out : 1'bz;  // Controlled_Buffer controlled_buffer_4
  assign out_23 = in_14 ? xor_13_out : 1'bz;  // Controlled_Buffer controlled_buffer_5
  assign out_24 = in_14 ? xor_14_out : 1'bz;  // Controlled_Buffer controlled_buffer_6
  assign out_25 = in_14 ? xor_15_out : 1'bz;  // Controlled_Buffer controlled_buffer_7
  assign out_26 = in_14 ? xor_16_out : 1'bz;  // Controlled_Buffer controlled_buffer_8
endmodule

module CPU (
  input  in_1,
  input  in_2,
  input  in_3,
  input  in_4,
  input  in_5,
  input  in_6,
  input  in_7,
  input  in_8,
  input  in_9,
  input  in_10,
  input  in_11,
  input  in_12,
  input  in_13,
  input  in_14,
  input  in_15,
  input  in_16,
  input  in_17,
  input  in_18,
  input  in_19,
  input  in_20,
  input  in_21,
  input  in_22,
  input  in_23,
  input  in_24,
  input  in_25,
  output out_26,
  output out_27,
  output out_28,
  output out_29,
  output out_30,
  output out_31,
  output out_32,
  output out_33
);

  wire register_a_1_out_13, register_a_1_out_14, register_a_1_out_15, register_a_1_out_16,
       register_a_1_out_17, register_a_1_out_18, register_a_1_out_19, register_a_1_out_20,
       register_b_1_out_14, register_b_1_out_15, register_b_1_out_16, register_b_1_out_17,
       register_b_1_out_18, register_b_1_out_19, register_b_1_out_20, register_b_1_out_21;

  Register_B register_b_1 (
    .in_1(in_12), .in_3(in_15), .in_4(in_14), .in_5(in_13), .in_6(in_16), .in_7(in_18), .in_8(in_19),
    .in_9(in_20), .in_10(in_21), .in_11(in_23), .in_12(in_24), .out_14(register_b_1_out_14),
    .out_15(register_b_1_out_15), .out_16(register_b_1_out_16), .out_21(register_b_1_out_21),
    .out_20(register_b_1_out_20), .out_19(register_b_1_out_19), .out_18(register_b_1_out_18),
    .out_17(register_b_1_out_17), .in_13(in_25), .in_2(in_17));
  Register_A register_a_1 (
    .in_2(in_5), .in_3(in_2), .in_4(in_1), .out_13(register_a_1_out_13), .in_5(in_3),
    .out_14(register_a_1_out_14), .in_6(in_4), .out_15(register_a_1_out_15), .in_7(in_6),
    .out_16(register_a_1_out_16), .in_8(in_7), .out_17(register_a_1_out_17), .in_9(in_8),
    .out_18(register_a_1_out_18), .in_10(in_9), .out_19(register_a_1_out_19), .in_11(in_10),
    .out_20(register_a_1_out_20), .in_12(in_11), .in_1(in_12));
  ALU alu_1 (
    .in_1(register_a_1_out_20), .in_2(register_b_1_out_21), .in_3(in_25), .in_4(register_a_1_out_19),
    .in_5(register_b_1_out_20), .in_6(register_a_1_out_18), .in_7(register_b_1_out_19),
    .in_8(register_a_1_out_17), .in_9(register_b_1_out_18), .in_10(register_a_1_out_16),
    .in_11(register_b_1_out_17), .in_12(register_a_1_out_15), .in_13(register_b_1_out_16), .in_14(in_22),
    .in_15(register_a_1_out_14), .in_16(register_b_1_out_15), .in_17(register_a_1_out_13),
    .in_18(register_b_1_out_14), .out_19(out_33), .out_20(out_32), .out_21(out_31), .out_22(out_30),
    .out_23(out_29), .out_24(out_28), .out_25(out_27), .out_26(out_26));  // open: out_27
endmodule

module _1_Bit_Data (
  input  EN,
  input  D,
  input  WR,
  output OUT
);

  wire and_1_out, and_2_out, and_3_out, and_4_out, nor_1_out, nor_2_out, not_1_out, not_2_out, or_1_out;

  not not_1 (not_1_out, EN);
  and and_1 (and_1_out, nor_1_out, not_1_out);
  and and_2 (and_2_out, EN, D);
  or or_1 (or_1_out, and_1_out, and_2_out);
  not not_2 (not_2_out, or_1_out);
  and and_3 (and_3_out, not_2_out, WR);
  and and_4 (and_4_out, WR, or_1_out);
  nor nor_1 (nor_1_out, and_3_out, nor_2_out);
  nor nor_2 (nor_2_out, nor_1_out, and_4_out);
  and and_5 (OUT, EN, nor_1_out);
endmodule

module _8_Bit_RAM (
  input  in_1,
  input  in_2,
  input  in_3,
  input  in_4,
  input  in_5,
  input  in_6,
  input  in_7,
  input  in_8,
  input  in_9,
  input  in_10,
  input  in_11,
  input  in_12,
  input  CS,
  input  RD,
  input  EO,
  output out_16,
  output out_17,
  output out_18,
  output out_19,
  output out_20,
  output out_21,
  output out_22,
  output out_23
);

  wire and_1_out, and_2_out, and_3_out, and_4_out, and_5_out, and_6_out, and_7_out, and_8_out, and_9_out,
       and_10_out, and_11_out, and_12_out, and_13_out, and_14_out, and_15_out, and_16_out, and_17_out,
       and_18_out, and_19_out, and_20_out, and_21_out, and_22_out, and_23_out, and_24_out, and_25_out,
       and_26_out, and_27_out, and_28_out, and_29_out, and_30_out, and_31_out, and_32_out, and_33_out,
       and_34_out, n1_bit_data_1_out, n1_bit_data_2_out, n1_bit_data_3_out, n1_bit_data_4_out,
       n1_bit_data_5_out, n1_bit_data_6_out, n1_bit_data_7_out, n1_bit_data_8_out, n1_bit_data_9_out,
       n1_bit_data_10_out, n1_bit_data_11_out, n1_bit_data_12_out, n1_bit_data_13_out, n1_bit_data_14_out,
       n1_bit_data_15_out, n1_bit_data_16_out, n1_bit_data_17_out, n1_bit_data_18_out, n1_bit_data_19_out,
       n1_bit_data_20_out, n1_bit_data_21_out, n1_bit_data_22_out, n1_bit_data_23_out, n1_bit_data_24_out,
       n1_bit_data_25_out, n1_bit_data_26_out, n1_bit_data_27_out, n1_bit_data_28_out, n1_bit_data_29_out,
       n1_bit_data_31_out, n1_bit_data_32_out, n1_bit_data_33_out, n1_bit_data_34_out, n1_bit_data_35_out,
       n1_bit_data_36_out, n1_bit_data_37_out, n1_bit_data_38_out, n1_bit_data_39_out, n1_bit_data_40_out,
       n1_bit_data_41_out, n1_bit_data_42_out, n1_bit_data_43_out, n1_bit_data_44_out, n1_bit_data_45_out,
       n1_bit_data_46_out, n1_bit_data_47_out, n1_bit_data_48_out, n1_bit_data_49_out, n1_bit_data_50_out,
       n1_bit_data_51_out, n1_bit_data_52_out, n1_bit_data_53_out, n1_bit_data_54_out, n1_bit_data_55_out,
       n1_bit_data_56_out, n1_bit_data_57_out, n1_bit_data_58_out, n1_bit_data_59_out, n1_bit_data_60_out,
       n1_bit_data_61_out, n1_bit_data_62_out, n1_bit_data_63_out, n1_bit_data_64_out, n1_bit_data_65_out,
       n1_bit_data_66_out, n1_bit_data_67_out, n1_bit_data_68_out, n1_bit_data_69_out, n1_bit_data_70_out,
       n1_bit_data_71_out, n1_bit_data_72_out, n1_bit_data_73_out, n1_bit_data_74_out, n1_bit_data_75_out,
       n1_bit_data_76_out, n1_bit_data_77_out, n1_bit_data_78_out, n1_bit_data_79_out, n1_bit_data_80_out,
       n1_bit_data_81_out, n1_bit_data_82_out, n1_bit_data_83_out, n1_bit_data_84_out, n1_bit_data_85_out,
       n1_bit_data_86_out, n1_bit_data_87_out, n1_bit_data_88_out, n1_bit_data_89_out, n1_bit_data_90_out,
       n1_bit_data_91_out, n1_bit_data_92_out, n1_bit_data_93_out, n1_bit_data_94_out, n1_bit_data_95_out,
       n1_bit_data_96_out, n1_bit_data_97_out, n1_bit_data_98_out, n1_bit_data_99_out, n1_bit_data_100_out,
       n1_bit_data_101_out, n1_bit_data_102_out, n1_bit_data_103_out, n1_bit_data_104_out,
       n1_bit_data_105_out, n1_bit_data_106_out, n1_bit_data_107_out, n1_bit_data_108_out,
       n1_bit_data_109_out, n1_bit_data_110_out, n1_bit_data_111_out, n1_bit_data_112_out,
       n1_bit_data_113_out, n1_bit_data_114_out, n1_bit_data_115_out, n1_bit_data_116_out,
       n1_bit_data_117_out, n1_bit_data_118_out, n1_bit_data_119_out, n1_bit_data_120_out,
       n1_bit_data_121_out, n1_bit_data_122_out, n1_bit_data_123_out, n1_bit_data_124_out,
       n1_bit_data_125_out, n1_bit_data_126_out, n1_bit_data_127_out, n1_bit_data_128_out, not_1_out,
       not_2_out, not_3_out, not_4_out, not_5_out, or_1_out, or_2_out, or_3_out, or_4_out, or_5_out,
       or_6_out, or_7_out, or_8_out;

  not not_1 (not_1_out, in_9);
  not not_2 (not_2_out, in_10);
  not not_3 (not_3_out, in_11);
  not not_4 (not_4_out, in_12);
  and and_1 (and_1_out, not_1_out, not_2_out, not_3_out, not_4_out);
  and and_2 (and_2_out, in_9, not_2_out, not_3_out, not_4_out);
  and and_3 (and_3_out, not_1_out, in_10, not_3_out, not_4_out);
  and and_4 (and_4_out, in_9, in_10, not_3_out, not_4_out);
  and and_5 (and_5_out, not_1_out, not_2_out, in_11, not_4_out);
  and and_6 (and_6_out, in_9, not_2_out, in_11, not_4_out);
  and and_7 (and_7_out, not_1_out, in_10, in_11, not_4_out);
  and and_8 (and_8_out, in_9, in_10, in_11, not_4_out);
  and and_9 (and_9_out, not_1_out, not_2_out, not_3_out, in_12);
  and and_10 (and_10_out, in_9, not_2_out, not_3_out, in_12);
  and and_11 (and_11_out, not_1_out, in_10, not_3_out, in_12);
  and and_12 (and_12_out, in_9, in_10, not_3_out, in_12);
  and and_13 (and_13_out, not_1_out, not_2_out, in_11, in_12);
  and and_14 (and_14_out, in_9, not_2_out, in_11, in_12);
  and and_15 (and_15_out, not_1_out, in_10, in_11, in_12);
  and and_16 (and_16_out, in_9, in_10, in_11, in_12);
  and and_17 (and_17_out, CS, not_5_out);
  and and_18 (and_18_out, and_17_out, and_1_out);
  and and_19 (and_19_out, and_17_out, and_2_out);
  and and_20 (and_20_out, and_17_out, and_3_out);
  and and_21 (and_21_out, and_17_out, and_4_out);
  and and_22 (and_22_out, and_17_out, and_5_out);
  and and_23 (and_23_out, and_17_out, and_6_out);
  and and_24 (and_24_out, and_17_out, and_7_out);
  and and_25 (and_25_out, and_17_out, and_8_out);
  and and_26 (and_26_out, and_17_out, and_9_out);
  and and_27 (and_27_out, and_17_out, and_10_out);
  and and_28 (and_28_out, and_17_out, and_11_out);
  and and_29 (and_29_out, and_17_out, and_12_out);
  and and_30 (and_30_out, and_17_out, and_13_out);
  and and_31 (and_31_out, and_17_out, and_14_out);
  and and_32 (and_32_out, and_17_out, and_15_out);
  and and_33 (and_33_out, and_17_out, and_16_out);
  not not_5 (not_5_out, RD);
  and and_34 (and_34_out, RD, EO);
  _1_Bit_Data u_1_bit_data_1 (.D(in_1), .WR(and_18_out), .OUT(n1_bit_data_1_out), .EN(and_1_out));
  _1_Bit_Data u_1_bit_data_2 (.D(in_1), .WR(and_19_out), .OUT(n1_bit_data_2_out), .EN(and_2_out));
  _1_Bit_Data u_1_bit_data_3 (.D(in_1), .WR(and_20_out), .OUT(n1_bit_data_3_out), .EN(and_3_out));
  _1_Bit_Data u_1_bit_data_4 (.D(in_1), .WR(and_21_out), .OUT(n1_bit_data_4_out), .EN(and_4_out));
  _1_Bit_Data u_1_bit_data_5 (.D(in_1), .WR(and_22_out), .OUT(n1_bit_data_5_out), .EN(and_5_out));
  _1_Bit_Data u_1_bit_data_6 (.D(in_1), .WR(and_23_out), .OUT(n1_bit_data_6_out), .EN(and_6_out));
  _1_Bit_Data u_1_bit_data_7 (.D(in_1), .WR(and_24_out), .OUT(n1_bit_data_7_out), .EN(and_7_out));
  _1_Bit_Data u_1_bit_data_8 (.D(in_1), .WR(and_25_out), .OUT(n1_bit_data_8_out), .EN(and_8_out));
  _1_Bit_Data u_1_bit_data_9 (.D(in_1), .WR(and_26_out), .OUT(n1_bit_data_9_out), .EN(and_9_out));
  _1_Bit_Data u_1_bit_data_10 (.D(in_1), .WR(and_27_out), .OUT(n1_bit_data_10_out), .EN(and_10_out));
  _1_Bit_Data u_1_bit_data_11 (.D(in_1), .WR(and_28_out), .OUT(n1_bit_data_11_out), .EN(and_11_out));
  _1_Bit_Data u_1_bit_data_12 (.D(in_1), .WR(and_29_out), .OUT(n1_bit_data_12_out), .EN(and_12_out));
  _1_Bit_Data u_1_bit_data_13 (.D(in_1), .WR(and_30_out), .OUT(n1_bit_data_13_out), .EN(and_13_out));
  _1_Bit_Data u_1_bit_data_14 (.D(in_1), .WR(and_31_out), .OUT(n1_bit_data_14_out), .EN(and_14_out));
  _1_Bit_Data u_1_bit_data_15 (.D(in_1), .WR(and_32_out), .OUT(n1_bit_data_15_out), .EN(and_15_out));
  _1_Bit_Data u_1_bit_data_16 (.D(in_1), .WR(and_33_out), .OUT(n1_bit_data_16_out), .EN(and_16_out));
  _1_Bit_Data u_1_bit_data_17 (.D(in_2), .WR(and_18_out), .OUT(n1_bit_data_17_out), .EN(and_1_out));
  _1_Bit_Data u_1_bit_data_18 (.D(in_2), .WR(and_19_out), .OUT(n1_bit_data_18_out), .EN(and_2_out));
  _1_Bit_Data u_1_bit_data_19 (.D(in_2), .WR(and_20_out), .OUT(n1_bit_data_19_out), .EN(and_3_out));
  _1_Bit_Data u_1_bit_data_20 (.D(in_2), .WR(and_21_out), .OUT(n1_bit_data_20_out), .EN(and_4_out));
  _1_Bit_Data u_1_bit_data_21 (.D(in_2), .WR(and_22_out), .OUT(n1_bit_data_21_out), .EN(and_5_out));
  _1_Bit_Data u_1_bit_data_22 (.D(in_2), .WR(and_23_out), .OUT(n1_bit_data_22_out), .EN(and_6_out));
  _1_Bit_Data u_1_bit_data_23 (.D(in_2), .WR(and_24_out), .OUT(n1_bit_data_23_out), .EN(and_7_out));
  _1_Bit_Data u_1_bit_data_24 (.D(in_2), .WR(and_25_out), .OUT(n1_bit_data_24_out), .EN(and_8_out));
  _1_Bit_Data u_1_bit_data_25 (.D(in_2), .WR(and_26_out), .OUT(n1_bit_data_25_out), .EN(and_9_out));
  _1_Bit_Data u_1_bit_data_26 (.D(in_2), .WR(and_27_out), .OUT(n1_bit_data_26_out), .EN(and_10_out));
  _1_Bit_Data u_1_bit_data_27 (.D(in_2), .WR(and_28_out), .OUT(n1_bit_data_27_out), .EN(and_11_out));
  _1_Bit_Data u_1_bit_data_28 (.D(in_2), .WR(and_29_out), .OUT(n1_bit_data_28_out), .EN(and_12_out));
  _1_Bit_Data u_1_bit_data_29 (.D(in_2), .WR(and_30_out), .OUT(n1_bit_data_29_out), .EN(and_13_out));
  _1_Bit_Data u_1_bit_data_30 (.D(in_2), .WR(and_31_out), .OUT(n1_bit_data_14_out), .EN(and_14_out));
  _1_Bit_Data u_1_bit_data_31 (.D(in_2), .WR(and_32_out), .OUT(n1_bit_data_31_out), .EN(and_15_out));
  _1_Bit_Data u_1_bit_data_32 (.D(in_2), .WR(and_33_out), .OUT(n1_bit_data_32_out), .EN(and_16_out));
  _1_Bit_Data u_1_bit_data_33 (.D(in_3), .WR(and_18_out), .OUT(n1_bit_data_33_out), .EN(and_1_out));
  _1_Bit_Data u_1_bit_data_34 (.D(in_3), .WR(and_19_out), .OUT(n1_bit_data_34_out), .EN(and_2_out));
  _1_Bit_Data u_1_bit_data_35 (.D(in_3), .WR(and_20_out), .OUT(n1_bit_data_35_out), .EN(and_3_out));
  _1_Bit_Data u_1_bit_data_36 (.D(in_3), .WR(and_21_out), .OUT(n1_bit_data_36_out), .EN(and_4_out));
  _1_Bit_Data u_1_bit_data_37 (.D(in_3), .WR(and_22_out), .OUT(n1_bit_data_37_out), .EN(and_5_out));
  _1_Bit_Data u_1_bit_data_38 (.D(in_3), .WR(and_23_out), .OUT(n1_bit_data_38_out), .EN(and_6_out));
  _1_Bit_Data u_1_bit_data_39 (.D(in_3), .WR(and_24_out), .OUT(n1_bit_data_39_out), .EN(and_7_out));
  _1_Bit_Data u_1_bit_data_40 (.D(in_3), .WR(and_25_out), .OUT(n1_bit_data_40_out), .EN(and_8_out));
  _1_Bit_Data u_1_bit_data_41 (.D(in_3), .WR(and_26_out), .OUT(n1_bit_data_41_out), .EN(and_9_out));
  _1_Bit_Data u_1_bit_data_42 (.D(in_3), .WR(and_27_out), .OUT(n1_bit_data_42_out), .EN(and_10_out));
  _1_Bit_Data u_1_bit_data_43 (.D(in_3), .WR(and_28_out), .OUT(n1_bit_data_43_out), .EN(and_11_out));
  _1_Bit_Data u_1_bit_data_44 (.D(in_3), .WR(and_29_out), .OUT(n1_bit_data_44_out), .EN(and_12_out));
  _1_Bit_Data u_1_bit_data_45 (.D(in_3), .WR(and_30_out), .OUT(n1_bit_data_45_out), .EN(and_13_out));
  _1_Bit_Data u_1_bit_data_46 (.D(in_3), .WR(and_31_out), .OUT(n1_bit_data_46_out), .EN(and_14_out));
  _1_Bit_Data u_1_bit_data_47 (.D(in_3), .WR(and_32_out), .OUT(n1_bit_data_47_out), .EN(and_15_out));
  _1_Bit_Data u_1_bit_data_48 (.D(in_3), .WR(and_33_out), .OUT(n1_bit_data_48_out), .EN(and_16_out));
  _1_Bit_Data u_1_bit_data_49 (.D(in_4), .WR(and_18_out), .OUT(n1_bit_data_49_out), .EN(and_1_out));
  _1_Bit_Data u_1_bit_data_50 (.D(in_4), .WR(and_19_out), .OUT(n1_bit_data_50_out), .EN(and_2_out));
  _1_Bit_Data u_1_bit_data_51 (.D(in_4), .WR(and_20_out), .OUT(n1_bit_data_51_out), .EN(and_3_out));
  _1_Bit_Data u_1_bit_data_52 (.D(in_4), .WR(and_21_out), .OUT(n1_bit_data_52_out), .EN(and_4_out));
  _1_Bit_Data u_1_bit_data_53 (.D(in_4), .WR(and_22_out), .OUT(n1_bit_data_53_out), .EN(and_5_out));
  _1_Bit_Data u_1_bit_data_54 (.D(in_4), .WR(and_23_out), .OUT(n1_bit_data_54_out), .EN(and_6_out));
  _1_Bit_Data u_1_bit_data_55 (.D(in_4), .WR(and_24_out), .OUT(n1_bit_data_55_out), .EN(and_7_out));
  _1_Bit_Data u_1_bit_data_56 (.D(in_4), .WR(and_25_out), .OUT(n1_bit_data_56_out), .EN(and_8_out));
  _1_Bit_Data u_1_bit_data_57 (.D(in_4), .WR(and_26_out), .OUT(n1_bit_data_57_out), .EN(and_9_out));
  _1_Bit_Data u_1_bit_data_58 (.D(in_4), .WR(and_27_out), .OUT(n1_bit_data_58_out), .EN(and_10_out));
  _1_Bit_Data u_1_bit_data_59 (.D(in_4), .WR(and_28_out), .OUT(n1_bit_data_59_out), .EN(and_11_out));
  _1_Bit_Data u_1_bit_data_60 (.D(in_4), .WR(and_29_out), .OUT(n1_bit_data_60_out), .EN(and_12_out));
  _1_Bit_Data u_1_bit_data_61 (.D(in_4), .WR(and_30_out), .OUT(n1_bit_data_61_out), .EN(and_13_out));
  _1_Bit_Data u_1_bit_data_62 (.D(in_4), .WR(and_31_out), .OUT(n1_bit_data_62_out), .EN(and_14_out));
  _1_Bit_Data u_1_bit_data_63 (.D(in_4), .WR(and_32_out), .OUT(n1_bit_data_63_out), .EN(and_15_out));
  _1_Bit_Data u_1_bit_data_64 (.D(in_4), .WR(and_33_out), .OUT(n1_bit_data_64_out), .EN(and_16_out));
  _1_Bit_Data u_1_bit_data_65 (.D(in_5), .WR(and_18_out), .OUT(n1_bit_data_65_out), .EN(and_1_out));
  _1_Bit_Data u_1_bit_data_66 (.D(in_5), .WR(and_19_out), .OUT(n1_bit_data_66_out), .EN(and_2_out));
  _1_Bit_Data u_1_bit_data_67 (.D(in_5), .WR(and_20_out), .OUT(n1_bit_data_67_out), .EN(and_3_out));
  _1_Bit_Data u_1_bit_data_68 (.D(in_5), .WR(and_21_out), .OUT(n1_bit_data_68_out), .EN(and_4_out));
  _1_Bit_Data u_1_bit_data_69 (.D(in_5), .WR(and_22_out), .OUT(n1_bit_data_69_out), .EN(and_5_out));
  _1_Bit_Data u_1_bit_data_70 (.D(in_5), .WR(and_23_out), .OUT(n1_bit_data_70_out), .EN(and_6_out));
  _1_Bit_Data u_1_bit_data_71 (.D(in_5), .WR(and_24_out), .OUT(n1_bit_data_71_out), .EN(and_7_out));
  _1_Bit_Data u_1_bit_data_72 (.D(in_5), .WR(and_25_out), .OUT(n1_bit_data_72_out), .EN(and_8_out));
  _1_Bit_Data u_1_bit_data_73 (.D(in_5), .WR(and_26_out), .OUT(n1_bit_data_73_out), .EN(and_9_out));
  _1_Bit_Data u_1_bit_data_74 (.D(in_5), .WR(and_27_out), .OUT(n1_bit_data_74_out), .EN(and_10_out));
  _1_Bit_Data u_1_bit_data_75 (.D(in_5), .WR(and_28_out), .OUT(n1_bit_data_75_out), .EN(and_11_out));
  _1_Bit_Data u_1_bit_data_76 (.D(in_5), .WR(and_29_out), .OUT(n1_bit_data_76_out), .EN(and_12_out));
  _1_Bit_Data u_1_bit_data_77 (.D(in_5), .WR(and_30_out), .OUT(n1_bit_data_77_out), .EN(and_13_out));
  _1_Bit_Data u_1_bit_data_78 (.D(in_5), .WR(and_31_out), .OUT(n1_bit_data_78_out), .EN(and_14_out));
  _1_Bit_Data u_1_bit_data_79 (.D(in_5), .WR(and_32_out), .OUT(n1_bit_data_79_out), .EN(and_15_out));
  _1_Bit_Data u_1_bit_data_80 (.D(in_5), .WR(and_33_out), .OUT(n1_bit_data_80_out), .EN(and_16_out));
  _1_Bit_Data u_1_bit_data_81 (.D(in_6), .WR(and_18_out), .OUT(n1_bit_data_81_out), .EN(and_1_out));
  _1_Bit_Data u_1_bit_data_82 (.D(in_6), .WR(and_19_out), .OUT(n1_bit_data_82_out), .EN(and_2_out));
  _1_Bit_Data u_1_bit_data_83 (.D(in_6), .WR(and_20_out), .OUT(n1_bit_data_83_out), .EN(and_3_out));
  _1_Bit_Data u_1_bit_data_84 (.D(in_6), .WR(and_21_out), .OUT(n1_bit_data_84_out), .EN(and_4_out));
  _1_Bit_Data u_1_bit_data_85 (.D(in_6), .WR(and_22_out), .OUT(n1_bit_data_85_out), .EN(and_5_out));
  _1_Bit_Data u_1_bit_data_86 (.D(in_6), .WR(and_23_out), .OUT(n1_bit_data_86_out), .EN(and_6_out));
  _1_Bit_Data u_1_bit_data_87 (.D(in_6), .WR(and_24_out), .OUT(n1_bit_data_87_out), .EN(and_7_out));
  _1_Bit_Data u_1_bit_data_88 (.D(in_6), .WR(and_25_out), .OUT(n1_bit_data_88_out), .EN(and_8_out));
  _1_Bit_Data u_1_bit_data_89 (.D(in_6), .WR(and_26_out), .OUT(n1_bit_data_89_out), .EN(and_9_out));
  _1_Bit_Data u_1_bit_data_90 (.D(in_6), .WR(and_27_out), .OUT(n1_bit_data_90_out), .EN(and_10_out));
  _1_Bit_Data u_1_bit_data_91 (.D(in_6), .WR(and_28_out), .OUT(n1_bit_data_91_out), .EN(and_11_out));
  _1_Bit_Data u_1_bit_data_92 (.D(in_6), .WR(and_29_out), .OUT(n1_bit_data_92_out), .EN(and_12_out));
  _1_Bit_Data u_1_bit_data_93 (.D(in_6), .WR(and_30_out), .OUT(n1_bit_data_93_out), .EN(and_13_out));
  _1_Bit_Data u_1_bit_data_94 (.D(in_6), .WR(and_31_out), .OUT(n1_bit_data_94_out), .EN(and_14_out));
  _1_Bit_Data u_1_bit_data_95 (.D(in_6), .WR(and_32_out), .OUT(n1_bit_data_95_out), .EN(and_15_out));
  _1_Bit_Data u_1_bit_data_96 (.D(in_6), .WR(and_33_out), .OUT(n1_bit_data_96_out), .EN(and_16_out));
  _1_Bit_Data u_1_bit_data_97 (.D(in_7), .WR(and_18_out), .OUT(n1_bit_data_97_out), .EN(and_1_out));
  _1_Bit_Data u_1_bit_data_98 (.D(in_7), .WR(and_19_out), .OUT(n1_bit_data_98_out), .EN(and_2_out));
  _1_Bit_Data u_1_bit_data_99 (.D(in_7), .WR(and_20_out), .OUT(n1_bit_data_99_out), .EN(and_3_out));
  _1_Bit_Data u_1_bit_data_100 (.D(in_7), .WR(and_21_out), .OUT(n1_bit_data_100_out), .EN(and_4_out));
  _1_Bit_Data u_1_bit_data_101 (.D(in_7), .WR(and_22_out), .OUT(n1_bit_data_101_out), .EN(and_5_out));
  _1_Bit_Data u_1_bit_data_102 (.D(in_7), .WR(and_23_out), .OUT(n1_bit_data_102_out), .EN(and_6_out));
  _1_Bit_Data u_1_bit_data_103 (.D(in_7), .WR(and_24_out), .OUT(n1_bit_data_103_out), .EN(and_7_out));
  _1_Bit_Data u_1_bit_data_104 (.D(in_7), .WR(and_25_out), .OUT(n1_bit_data_104_out), .EN(and_8_out));
  _1_Bit_Data u_1_bit_data_105 (.D(in_7), .WR(and_26_out), .OUT(n1_bit_data_105_out), .EN(and_9_out));
  _1_Bit_Data u_1_bit_data_106 (.D(in_7), .WR(and_27_out), .OUT(n1_bit_data_106_out), .EN(and_10_out));
  _1_Bit_Data u_1_bit_data_107 (.D(in_7), .WR(and_28_out), .OUT(n1_bit_data_107_out), .EN(and_11_out));
  _1_Bit_Data u_1_bit_data_108 (.D(in_7), .WR(and_29_out), .OUT(n1_bit_data_108_out), .EN(and_12_out));
  _1_Bit_Data u_1_bit_data_109 (.D(in_7), .WR(and_30_out), .OUT(n1_bit_data_109_out), .EN(and_13_out));
  _1_Bit_Data u_1_bit_data_110 (.D(in_7), .WR(and_31_out), .OUT(n1_bit_data_110_out), .EN(and_14_out));
  _1_Bit_Data u_1_bit_data_111 (.D(in_7), .WR(and_32_out), .OUT(n1_bit_data_111_out), .EN(and_15_out));
  _1_Bit_Data u_1_bit_data_112 (.D(in_7), .WR(and_33_out), .OUT(n1_bit_data_112_out), .EN(and_16_out));
  _1_Bit_Data u_1_bit_data_113 (.D(in_8), .WR(and_18_out), .OUT(n1_bit_data_113_out), .EN(and_1_out));
  _1_Bit_Data u_1_bit_data_114 (.D(in_8), .WR(and_19_out), .OUT(n1_bit_data_114_out), .EN(and_2_out));
  _1_Bit_Data u_1_bit_data_115 (.D(in_8), .WR(and_20_out), .OUT(n1_bit_data_115_out), .EN(and_3_out));
  _1_Bit_Data u_1_bit_data_116 (.D(in_8), .WR(and_21_out), .OUT(n1_bit_data_116_out), .EN(and_4_out));
  _1_Bit_Data u_1_bit_data_117 (.D(in_8), .WR(and_22_out), .OUT(n1_bit_data_117_out), .EN(and_5_out));
  _1_Bit_Data u_1_bit_data_118 (.D(in_8), .WR(and_23_out), .OUT(n1_bit_data_118_out), .EN(and_6_out));
  _1_Bit_Data u_1_bit_data_119 (.D(in_8), .WR(and_24_out), .OUT(n1_bit_data_119_out), .EN(and_7_out));
  _1_Bit_Data u_1_bit_data_120 (.D(in_8), .WR(and_25_out), .OUT(n1_bit_data_120_out), .EN(and_8_out));
  _1_Bit_Data u_1_bit_data_121 (.D(in_8), .WR(and_26_out), .OUT(n1_bit_data_121_out), .EN(and_9_out));
  _1_Bit_Data u_1_bit_data_122 (.D(in_8), .WR(and_27_out), .OUT(n1_bit_data_122_out), .EN(and_10_out));
  _1_Bit_Data u_1_bit_data_123 (.D(in_8), .WR(and_28_out), .OUT(n1_bit_data_123_out), .EN(and_11_out));
  _1_Bit_Data u_1_bit_data_124 (.D(in_8), .WR(and_29_out), .OUT(n1_bit_data_124_out), .EN(and_12_out));
  _1_Bit_Data u_1_bit_data_125 (.D(in_8), .WR(and_30_out), .OUT(n1_bit_data_125_out), .EN(and_13_out));
  _1_Bit_Data u_1_bit_data_126 (.D(in_8), .WR(and_31_out), .OUT(n1_bit_data_126_out), .EN(and_14_out));
  _1_Bit_Data u_1_bit_data_127 (.D(in_8), .WR(and_32_out), .OUT(n1_bit_data_127_out), .EN(and_15_out));
  _1_Bit_Data u_1_bit_data_128 (.D(in_8), .WR(and_33_out), .OUT(n1_bit_data_128_out), .EN(and_16_out));
  or or_1 (or_1_out, n1_bit_data_1_out, n1_bit_data_2_out, n1_bit_data_3_out, n1_bit_data_4_out, n1_bit_data_5_out, n1_bit_data_6_out, n1_bit_data_7_out, n1_bit_data_8_out, n1_bit_data_9_out, n1_bit_data_10_out, n1_bit_data_11_out, n1_bit_data_12_out, n1_bit_data_13_out, n1_bit_data_14_out, n1_bit_data_15_out, n1_bit_data_16_out);
  or or_2 (or_2_out, n1_bit_data_17_out, n1_bit_data_18_out, n1_bit_data_19_out, n1_bit_data_20_out, n1_bit_data_21_out, n1_bit_data_22_out, n1_bit_data_23_out, n1_bit_data_24_out, n1_bit_data_25_out, n1_bit_data_26_out, n1_bit_data_27_out, n1_bit_data_28_out, n1_bit_data_29_out, n1_bit_data_14_out, n1_bit_data_31_out, n1_bit_data_32_out);
  or or_3 (or_3_out, n1_bit_data_33_out, n1_bit_data_34_out, n1_bit_data_35_out, n1_bit_data_36_out, n1_bit_data_37_out, n1_bit_data_38_out, n1_bit_data_39_out, n1_bit_data_40_out, n1_bit_data_41_out, n1_bit_data_42_out, n1_bit_data_43_out, n1_bit_data_44_out, n1_bit_data_45_out, n1_bit_data_46_out, n1_bit_data_47_out, n1_bit_data_48_out);
  or or_4 (or_4_out, n1_bit_data_49_out, n1_bit_data_50_out, n1_bit_data_51_out, n1_bit_data_52_out, n1_bit_data_53_out, n1_bit_data_54_out, n1_bit_data_55_out, n1_bit_data_56_out, n1_bit_data_57_out, n1_bit_data_58_out, n1_bit_data_59_out, n1_bit_data_60_out, n1_bit_data_61_out, n1_bit_data_62_out, n1_bit_data_63_out, n1_bit_data_64_out);
  or or_5 (or_5_out, n1_bit_data_65_out, n1_bit_data_66_out, n1_bit_data_67_out, n1_bit_data_68_out, n1_bit_data_69_out, n1_bit_data_70_out, n1_bit_data_71_out, n1_bit_data_72_out, n1_bit_data_73_out, n1_bit_data_74_out, n1_bit_data_75_out, n1_bit_data_76_out, n1_bit_data_77_out, n1_bit_data_78_out, n1_bit_data_79_out, n1_bit_data_80_out);
  or or_6 (or_6_out, n1_bit_data_81_out, n1_bit_data_82_out, n1_bit_data_83_out, n1_bit_data_84_out, n1_bit_data_85_out, n1_bit_data_86_out, n1_bit_data_87_out, n1_bit_data_88_out, n1_bit_data_89_out, n1_bit_data_90_out, n1_bit_data_91_out, n1_bit_data_92_out, n1_bit_data_93_out, n1_bit_data_94_out, n1_bit_data_95_out, n1_bit_data_96_out);
  or or_7 (or_7_out, n1_bit_data_97_out, n1_bit_data_98_out, n1_bit_data_99_out, n1_bit_data_100_out, n1_bit_data_101_out, n1_bit_data_102_out, n1_bit_data_103_out, n1_bit_data_104_out, n1_bit_data_105_out, n1_bit_data_106_out, n1_bit_data_107_out, n1_bit_data_108_out, n1_bit_data_109_out, n1_bit_data_110_out, n1_bit_data_111_out, n1_bit_data_112_out);
  or or_8 (or_8_out, n1_bit_data_113_out, n1_bit_data_114_out, n1_bit_data_115_out, n1_bit_data_116_out, n1_bit_data_117_out, n1_bit_data_118_out, n1_bit_data_119_out, n1_bit_data_120_out, n1_bit_data_121_out, n1_bit_data_122_out, n1_bit_data_123_out, n1_bit_data_124_out, n1_bit_data_125_out, n1_bit_data_126_out, n1_bit_data_127_out, n1_bit_data_128_out);
  assign out_16 = and_34_out ? or_1_out : 1'bz;  // Controlled_Buffer controlled_buffer_1
  assign out_17 = and_34_out ? or_2_out : 1'bz;  // Controlled_Buffer controlled_buffer_2
  assign out_18 = and_34_out ? or_3_out : 1'bz;  // Controlled_Buffer controlled_buffer_3
  assign out_19 = and_34_out ? or_4_out : 1'bz;  // Controlled_Buffer controlled_buffer_4
  assign out_20 = and_34_out ? or_5_out : 1'bz;  // Controlled_Buffer controlled_buffer_5
  assign out_21 = and_34_out ? or_6_out : 1'bz;  // Controlled_Buffer controlled_buffer_6
  assign out_22 = and_34_out ? or_7_out : 1'bz;  // Controlled_Buffer controlled_buffer_7
  assign out_23 = and_34_out ? or_8_out : 1'bz;  // Controlled_Buffer controlled_buffer_8
endmodule
